// Logisim project 16-Bit ALU.circ as structural Verilog: 1 circuit, main circuit ALU
module ALU (
  input  [15:0] input_1,
  input  [15:0] input_2,
  input  [2:0] alu_op,
  input  alu_en,
  output carry_out,
  output [15:0] \output ,
  output Zero_flag
);

  wire adder_1_cout, comparator_1_lt, subtractor_1_bout;
  wire [15:0] adder_1_out, and_1_out, bit_extender_1_out, nor_1_out, or_1_out, subtractor_1_out, xor_1_out;

  Comparator #(.width(16)) comparator_1 (.a(input_1), .b(input_2), .lt(comparator_1_lt));  // open: gt, eq
  assign and_1_out = input_1 & input_2;  // AND_Gate and_1, 16 bits wide
  assign or_1_out = input_1 | input_2;  // OR_Gate or_1, 16 bits wide
  assign nor_1_out = ~(input_1 | input_2);  // NOR_Gate nor_1, 16 bits wide
  assign xor_1_out = input_1 ^ input_2;  // XOR_Gate xor_1, 16 bits wide
  Adder #(.width(16)) adder_1 (.a(input_1), .b(input_2), .out(adder_1_out), .cout(adder_1_cout));  // open: cin
  Subtractor #(.width(16)) subtractor_1 (
    .a(input_1), .b(input_2), .out(subtractor_1_out), .bout(subtractor_1_bout));  // open: bin
  assign bit_extender_1_out = {{15{1'b0}}, comparator_1_lt};  // Bit_Extender bit_extender_1
  Multiplexer multiplexer_1 (
    .in0(adder_1_cout), .in1(subtractor_1_bout), .out(carry_out), .sel(alu_op[0]), .en(alu_op[2]));
  Multiplexer #(.select(3), .width(16)) multiplexer_2 (
    .in0(and_1_out), .in1(or_1_out), .in2(nor_1_out), .in3(xor_1_out), .in4(adder_1_out),
    .in5(bit_extender_1_out), .in6(subtractor_1_out), .in7(adder_1_out), .out(\output ), .sel(alu_op),
    .en(alu_en));
  nor nor_2 (Zero_flag, \output [0], \output [1], \output [2], \output [3], \output [4], \output [5], \output [6], \output [7], \output [8], \output [9], \output [10], \output [11], \output [12], \output [13], \output [14], \output [15]);

  // Notes on the sheet:
  //   RD
endmodule
