// Logisim project ALU_CTRL.circ as structural Verilog: 1 circuit, main circuit ALU_CTRL
module ALU_CTRL (
  input  [3:0] opcode,
  input  [2:0] func,
  output [2:0] op
);

  wire and_1_out, and_2_out, and_3_out, and_4_out, and_5_out, and_6_out, and_7_out, and_8_out, not_1_out,
       not_2_out, not_3_out, not_4_out, not_5_out, not_6_out, not_7_out, not_8_out, not_9_out, not_10_out,
       not_11_out, not_12_out;

  not not_1 (not_1_out, opcode[0]);
  not not_2 (not_2_out, opcode[1]);
  not not_3 (not_3_out, opcode[2]);
  not not_4 (not_4_out, opcode[3]);
  not not_5 (not_5_out, opcode[0]);
  not not_6 (not_6_out, opcode[1]);
  not not_7 (not_7_out, opcode[2]);
  not not_8 (not_8_out, opcode[3]);
  not not_9 (not_9_out, opcode[0]);
  not not_10 (not_10_out, opcode[0]);
  and and_1 (and_1_out, not_1_out, not_2_out, not_3_out, not_4_out, func[0]);
  not not_11 (not_11_out, opcode[2]);
  and and_2 (and_2_out, opcode[1], not_11_out, opcode[3]);
  not not_12 (not_12_out, opcode[2]);
  and and_3 (and_3_out, opcode[0], not_12_out, opcode[3]);
  and and_4 (and_4_out, opcode[0], opcode[1]);
  and and_5 (and_5_out, not_5_out, not_6_out, not_7_out, not_8_out, func[1]);
  and and_6 (and_6_out, opcode[0], opcode[2]);
  and and_7 (and_7_out, not_9_out, func[2]);
  and and_8 (and_8_out, not_10_out, opcode[3]);
  or or_1 (op[0], and_1_out, and_2_out, and_3_out, and_4_out);
  or or_2 (op[1], and_5_out, and_6_out);
  or or_3 (op[2], and_7_out, and_8_out, opcode[2], opcode[1]);
endmodule
