// Logisim project Control-Unit.circ as structural Verilog: 1 circuit, main circuit Control
module Control (
  input  [3:0] opcode,
  output reg_WR,
  output mem_RD,
  output mem_WR,
  output MemtoReg,
  output ALU_EN,
  output ALU_src,
  output LUI,
  output JUMP,
  output BEQ,
  output BNE,
  output JAL,
  output RegDEST,
  output LH_LB,
  output HALF,
  output SIN
);

  wire and_2_out, and_3_out, and_4_out, and_5_out, and_7_out, and_8_out, and_9_out, and_10_out, and_11_out,
       and_12_out, and_13_out, and_14_out, and_15_out, not_1_out, not_2_out, not_3_out, not_4_out, not_5_out,
       not_6_out, not_7_out, not_8_out, not_9_out, not_10_out, not_11_out, not_12_out, not_13_out,
       not_14_out, not_15_out, not_16_out, not_17_out, not_18_out, not_19_out, not_20_out, not_21_out,
       not_22_out, not_23_out, not_24_out, not_25_out, not_26_out, not_27_out, not_28_out, not_29_out;

  not not_1 (not_1_out, opcode[0]);
  not not_2 (not_2_out, opcode[3]);
  not not_3 (not_3_out, opcode[1]);
  not not_4 (not_4_out, opcode[2]);
  not not_5 (not_5_out, opcode[2]);
  not not_6 (not_6_out, opcode[2]);
  not not_7 (not_7_out, opcode[3]);
  not not_8 (not_8_out, opcode[0]);
  not not_9 (not_9_out, opcode[0]);
  not not_10 (not_10_out, opcode[1]);
  not not_11 (not_11_out, opcode[2]);
  not not_12 (not_12_out, opcode[0]);
  not not_13 (not_13_out, opcode[3]);
  not not_14 (not_14_out, opcode[0]);
  not not_15 (not_15_out, opcode[1]);
  not not_16 (not_16_out, opcode[0]);
  not not_17 (not_17_out, opcode[0]);
  not not_18 (not_18_out, opcode[0]);
  not not_19 (not_19_out, opcode[1]);
  not not_20 (not_20_out, opcode[2]);
  and and_1 (LUI, opcode[0], opcode[1], opcode[2]);
  not not_21 (not_21_out, opcode[2]);
  not not_22 (not_22_out, opcode[3]);
  not not_23 (not_23_out, opcode[1]);
  not not_24 (not_24_out, opcode[1]);
  not not_25 (not_25_out, opcode[2]);
  not not_26 (not_26_out, opcode[0]);
  not not_27 (not_27_out, opcode[1]);
  not not_28 (not_28_out, opcode[2]);
  not not_29 (not_29_out, opcode[3]);
  and and_2 (and_2_out, not_1_out, not_2_out);
  and and_3 (and_3_out, not_3_out, not_4_out);
  and and_4 (and_4_out, not_5_out, opcode[3]);
  and and_5 (and_5_out, opcode[0], opcode[1], opcode[2]);
  or or_1 (mem_RD, not_6_out, not_7_out);
  and and_6 (mem_WR, not_8_out, opcode[2], opcode[3]);
  and and_7 (and_7_out, not_9_out, not_10_out, not_11_out, opcode[3]);
  and and_8 (and_8_out, not_12_out, opcode[2], not_13_out);
  or or_2 (ALU_EN, not_14_out, not_15_out);
  and and_9 (and_9_out, not_16_out, opcode[3]);
  and and_10 (and_10_out, not_17_out, opcode[2]);
  and and_11 (and_11_out, not_18_out, opcode[1]);
  and and_12 (and_12_out, opcode[1], opcode[2]);
  and and_13 (and_13_out, opcode[0], not_19_out, not_20_out);
  and and_14 (and_14_out, opcode[0], opcode[1], not_21_out);
  or or_3 (JUMP, and_14_out, and_15_out);
  and and_15 (and_15_out, opcode[0], opcode[1], not_22_out);
  and and_16 (BEQ, opcode[0], not_23_out, opcode[2]);
  and and_17 (BNE, opcode[0], not_24_out, opcode[2], opcode[3]);
  and and_18 (JAL, opcode[0], opcode[1], not_25_out, opcode[3]);
  and and_19 (RegDEST, not_26_out, not_27_out, not_28_out, not_29_out);
  not not_30 (LH_LB, opcode[2]);
  not not_31 (HALF, opcode[1]);
  or or_4 (reg_WR, and_2_out, and_3_out, and_4_out, and_5_out);
  or or_5 (MemtoReg, and_7_out, and_8_out);
  or or_6 (ALU_src, and_9_out, and_10_out, and_11_out, and_12_out, and_13_out);

  assign SIN = HALF;

  // Notes on the sheet:
  //   op2
  //   op1
endmodule
