// Logisim project Control_Source.circ as structural Verilog: 1 circuit, main circuit main
module main (
  input  in_1,
  input  in_2,
  input  in_3,
  input  in_4,
  input  in_5,
  input  in_6,
  input  in_7,
  input  in_8,
  input  in_9,
  input  in_10,
  input  in_11,
  input  in_12,
  input  in_13,
  input  in_14,
  input  stall,
  output out_16,
  output out_17,
  output out_18,
  output out_19,
  output out_20,
  output out_21,
  output out_22,
  output out_23,
  output out_24,
  output out_25,
  output out_26,
  output out_27,
  output out_28,
  output out_29
);

  Multiplexer #(.width(14), .enable("false")) multiplexer_1 (
    .in0({in_14, in_13, in_12, in_11, in_10, in_9, in_8, in_7, in_6, in_5, in_4, in_3, in_2, in_1}),
    .in1({14{1'b0}}),
    .out({out_29, out_28, out_27, out_26, out_25, out_24, out_23, out_22, out_21, out_20, out_19, out_18, out_17, out_16}),
    .sel(stall));
endmodule
