// Logisim project FINAL-CPU.circ as structural Verilog: 1 circuit, main circuit main
module main (
);

  wire alu_1_zero_flag, clock_1_out, control_1_alu_en, control_1_alu_src, control_1_beq, control_1_bne,
       control_1_half, control_1_jal, control_1_jump, control_1_lh_lb, control_1_lui, control_1_mem_rd,
       control_1_mem_wr, control_1_memtoreg, control_1_reg_wr, control_1_regdest, control_1_sin,
       main_2_pc_src;
  wire [2:0] alu_ctrl_1_op, inst_mem_1_instruction_2, inst_mem_1_instruction_3, multiplexer_2_out,
       multiplexer_3_out, multiplexer_4_out;
  wire [3:0] inst_mem_1_instruction_4;
  wire [5:0] inst_mem_1_instruction;
  wire [15:0] adder_1_out, alu_1_output, bit_extender_1_out, data_mem_1_output, main_1_shifted_imm,
       main_2_target_addr, main_3_inverse, main_4_lh_or_lb, multiplexer_1_out, multiplexer_5_out,
       multiplexer_6_out, multiplexer_7_out, multiplexer_8_out, multiplexer_9_out, PC_q,
       register_file_1_read_data1, register_file_1_read_data2;

  Multiplexer #(.width(16), .enable("false")) multiplexer_1 (
    .in0(adder_1_out), .in1(main_2_target_addr), .out(multiplexer_1_out), .sel(main_2_pc_src));
  Register #(.width(16)) PC (.D(multiplexer_1_out), .Q(PC_q), .clk(clock_1_out));  // open: en, clr
  Clock clock_1 (.out(clock_1_out));
  Adder #(.width(16)) adder_1 (.a(PC_q), .b(16'h1), .out(adder_1_out));  // open: cin, cout
  Inst_Mem inst_mem_1 (
    .Read_Address(PC_q),
    .Instruction({inst_mem_1_instruction_4, inst_mem_1_instruction_3, inst_mem_1_instruction_2, inst_mem_1_instruction}),
    .clk(clock_1_out));
  Multiplexer #(.width(3), .enable("false")) multiplexer_2 (
    .in0(inst_mem_1_instruction_2), .in1(inst_mem_1_instruction[5:3]), .out(multiplexer_2_out),
    .sel(control_1_regdest));
  Control control_1 (
    .reg_WR(control_1_reg_wr), .mem_RD(control_1_mem_rd), .mem_WR(control_1_mem_wr),
    .MemtoReg(control_1_memtoreg), .ALU_EN(control_1_alu_en), .ALU_src(control_1_alu_src),
    .LUI(control_1_lui), .JUMP(control_1_jump), .BEQ(control_1_beq), .BNE(control_1_bne),
    .JAL(control_1_jal), .RegDEST(control_1_regdest), .LH_LB(control_1_lh_lb), .HALF(control_1_half),
    .SIN(control_1_sin), .opcode(inst_mem_1_instruction_4));
  Multiplexer #(.width(3), .enable("false")) multiplexer_3 (
    .in0(multiplexer_4_out), .in1(3'b111), .out(multiplexer_3_out), .sel(control_1_jal));
  Multiplexer #(.width(3), .enable("false")) multiplexer_4 (
    .in0(multiplexer_2_out), .in1(3'b001), .out(multiplexer_4_out), .sel(control_1_lui));
  Register_File register_file_1 (
    .WriteData(multiplexer_5_out), .reg_Wr(control_1_reg_wr), .CLK(clock_1_out),
    .Write_Register(multiplexer_3_out), .Read_Data1(register_file_1_read_data1),
    .Read_Data2(register_file_1_read_data2), .R1(inst_mem_1_instruction_3), .R2(inst_mem_1_instruction_2));
  ALU_CTRL alu_ctrl_1 (.opcode(inst_mem_1_instruction_4), .func(inst_mem_1_instruction[2:0]), .op(alu_ctrl_1_op));
  Multiplexer #(.width(16), .enable("false")) multiplexer_5 (
    .in0(multiplexer_7_out), .in1(adder_1_out), .out(multiplexer_5_out), .sel(control_1_jal));
  assign bit_extender_1_out = {{10{inst_mem_1_instruction[5]}}, inst_mem_1_instruction};  // Bit_Extender bit_extender_1
  Multiplexer #(.width(16), .enable("false")) multiplexer_6 (
    .in0(register_file_1_read_data2), .in1(bit_extender_1_out), .out(multiplexer_6_out),
    .sel(control_1_alu_src));
  Multiplexer #(.width(16), .enable("false")) multiplexer_7 (
    .in0(multiplexer_9_out), .in1(main_1_shifted_imm), .out(multiplexer_7_out), .sel(control_1_lui));
  LUI_VALUE_main main_1 (
    .imm12({inst_mem_1_instruction_3, inst_mem_1_instruction_2, inst_mem_1_instruction}),
    .shifted_imm(main_1_shifted_imm));
  ALU alu_1 (
    .input_1(register_file_1_read_data1), .input_2(multiplexer_6_out), .alu_op(alu_ctrl_1_op),
    .\output (alu_1_output), .alu_en(control_1_alu_en), .Zero_flag(alu_1_zero_flag));  // open: carry_out
  next_pc_main main_2 (
    .incremented_pc(adder_1_out),
    .imm_12({inst_mem_1_instruction_3, inst_mem_1_instruction_2, inst_mem_1_instruction}),
    .BEQ(control_1_beq), .BNE(control_1_bne), .JUMP(control_1_jump), .target_addr(main_2_target_addr),
    .PC_SRC(main_2_pc_src), .ZERO(alu_1_zero_flag));
  SIN_main main_3 (.store_value(register_file_1_read_data2), .SIN(control_1_sin), .inverse(main_3_inverse));
  Data_Mem data_mem_1 (
    .Address(alu_1_output), .mem_RD(control_1_mem_rd), .mem_WR(control_1_mem_wr), .WriteData(main_3_inverse),
    .Output(data_mem_1_output), .clk(clock_1_out));
  Multiplexer #(.width(16), .enable("false")) multiplexer_8 (
    .in0(alu_1_output), .in1(data_mem_1_output), .out(multiplexer_8_out), .sel(control_1_memtoreg));
  Multiplexer #(.width(16), .enable("false")) multiplexer_9 (
    .in0(multiplexer_8_out), .in1(main_4_lh_or_lb), .out(multiplexer_9_out), .sel(control_1_half));
  lh_lb_main main_4 (.lh_lb(control_1_lh_lb), .Load_Value(multiplexer_8_out), .lh_or_lb(main_4_lh_or_lb));

  // Notes on the sheet:
  //   next pc
  //   pc+1
  //   +1
  //   R-TYPE
  //   imm 12
  //   I-TYPE
  //   imm6
  //   Rt
  //   RD
  //   LUI
  //   FUNC
  //   jal
  //   pc+1
  //   LUI
  //   zero
  //   Reg(Rt)
  //   alu result
  //   load result
  //   load val
  //   lowr bye/half
  //   half
endmodule
