// Logisim project FINAL-CPU_multi.circ as structural Verilog: 1 circuit, main circuit main
module main (
);

  wire alu_1_zero_flag, clock_1_out, control_1_alu_en, control_1_alu_src, control_1_beq, control_1_bne,
       control_1_half, control_1_jal, control_1_jump, control_1_lh_lb, control_1_lui, control_1_mem_rd,
       control_1_mem_wr, control_1_memtoreg, control_1_reg_wr, control_1_regdest, control_1_sin,
       ex_mem_1_beq_out, ex_mem_1_bneq_out, ex_mem_1_half_out, ex_mem_1_jump_out, ex_mem_1_lh_lb_out,
       ex_mem_1_lui_2, ex_mem_1_mem_rd_out, ex_mem_1_mem_wr_out, ex_mem_1_memtoreg_out, ex_mem_1_reg_wr_out,
       ex_mem_1_sin_out, ex_mem_1_zero_out, id_ex_1_alu_en_out, id_ex_1_alu_src_out, id_ex_1_beq_out,
       id_ex_1_bneq_out, id_ex_1_half_out, id_ex_1_jal_out, id_ex_1_jump_out, id_ex_1_lh_lb_out,
       id_ex_1_lui_out, id_ex_1_mem_rd_out, id_ex_1_mem_wr_out, id_ex_1_memtoreg_out, id_ex_1_reg_dest_out,
       id_ex_1_reg_wr_2, id_ex_1_sin_out, main_2_pc_src, mem_wb_1_half_out, mem_wb_1_lh_lb_out,
       mem_wb_1_lui_2, mem_wb_1_memtoreg_out, mem_wb_1_reg_wr_out, mem_wb_1_sin_out;
  wire [2:0] alu_ctrl_1_op, ex_mem_1_wr_reg_out, id_ex_1_bits3_5_out, id_ex_1_bits6_8_out, id_ex_1_func_out,
       if_id_1_instruction_out_2, if_id_1_instruction_out_3, mem_wb_1_wr_reg_out, write_reg_control_1_wr_reg;
  wire [3:0] id_ex_1_opcode_in_2;
  wire [5:0] if_id_1_instruction_out;
  wire [11:0] ex_mem_1_imm12_out, id_ex_1_imm12_out, id_ex_1_imm12_out_2;
  wire [15:0] adder_1_out, alu_1_output, bit_extender_1_out, data_mem_1_output, ex_mem_1_lui_shifted_2,
       ex_mem_1_pc_1_out, ex_mem_1_res_out, ex_mem_1_storevalue_out, id_ex_1_imm6ext16_out,
       id_ex_1_input1_out, id_ex_1_input2_out, id_ex_1_pc_1_out, if_id_1_pc_1_out, inst_mem_1_instruction,
       main_1_shifted_imm, main_2_target_addr, main_3_inverse, main_4_lh_or_lb, mem_wb_1_alu_res_out,
       mem_wb_1_loadres_out, mem_wb_1_lui_res_out, multiplexer_1_out, multiplexer_2_out, multiplexer_3_out,
       multiplexer_4_out, multiplexer_5_out, multiplexer_6_out, PC_q, register_file_1_read_data1,
       register_file_1_read_data2;
  wire [15:12] if_id_1_instruction_out_4;

  Clock clock_1 (.out(clock_1_out));
  Register #(.width(16)) PC (.D(multiplexer_1_out), .Q(PC_q), .clk(clock_1_out));  // open: en, clr
  Multiplexer #(.width(16), .enable("false")) multiplexer_1 (
    .in0(adder_1_out), .in1(main_2_target_addr), .out(multiplexer_1_out), .sel(main_2_pc_src));
  Adder #(.width(16)) adder_1 (.a(PC_q), .b(16'h1), .out(adder_1_out));  // open: cin, cout
  Inst_Mem inst_mem_1 (.Read_Address(PC_q), .Instruction(inst_mem_1_instruction), .clk(clock_1_out));
  IF_ID if_id_1 (
    .PC_1_in(adder_1_out), .PC_1_out(if_id_1_pc_1_out), .Instruction_in(inst_mem_1_instruction),
    .Instruction_out({if_id_1_instruction_out_4, if_id_1_instruction_out_3, if_id_1_instruction_out_2, if_id_1_instruction_out}),
    .CLK(clock_1_out));
  Control control_1 (
    .reg_WR(control_1_reg_wr), .mem_RD(control_1_mem_rd), .mem_WR(control_1_mem_wr),
    .MemtoReg(control_1_memtoreg), .ALU_EN(control_1_alu_en), .ALU_src(control_1_alu_src),
    .LUI(control_1_lui), .JUMP(control_1_jump), .BEQ(control_1_beq), .BNE(control_1_bne),
    .JAL(control_1_jal), .RegDEST(control_1_regdest), .LH_LB(control_1_lh_lb), .HALF(control_1_half),
    .SIN(control_1_sin), .opcode(if_id_1_instruction_out_4));
  Register_File register_file_1 (
    .WriteData(multiplexer_2_out), .reg_Wr(mem_wb_1_reg_wr_out), .CLK(clock_1_out),
    .Write_Register(mem_wb_1_wr_reg_out), .Read_Data1(register_file_1_read_data1),
    .Read_Data2(register_file_1_read_data2), .R1(if_id_1_instruction_out_3), .R2(if_id_1_instruction_out_2));
  Multiplexer #(.width(16), .enable("false")) multiplexer_2 (
    .in0(multiplexer_4_out), .in1(adder_1_out), .out(multiplexer_2_out), .sel(control_1_jal));
  assign bit_extender_1_out = {{10{if_id_1_instruction_out[5]}}, if_id_1_instruction_out};  // Bit_Extender bit_extender_1
  ID_EX id_ex_1 (
    .Target_address(if_id_1_pc_1_out),
    .imm12({if_id_1_instruction_out_3, if_id_1_instruction_out_2, if_id_1_instruction_out}),
    .mem_RD(control_1_mem_rd), .mem_WR(control_1_mem_wr), .MemToReg(control_1_memtoreg),
    .ALU_EN(control_1_alu_en), .ALU_src(control_1_alu_src), .LUI(control_1_lui), .JUMP(control_1_jump),
    .BEQ(control_1_beq), .BNEQ(control_1_bne), .LH_LB(control_1_lh_lb), .half(control_1_half),
    .sin(control_1_sin),
    .imm12_2({if_id_1_instruction_out_3, if_id_1_instruction_out_2, if_id_1_instruction_out}),
    .input1_in(register_file_1_read_data1), .input2_in(register_file_1_read_data2),
    .imm6ext16_in(bit_extender_1_out), .opcode_in(if_id_1_instruction_out_4),
    .func_in(if_id_1_instruction_out[2:0]), .CLK(clock_1_out), .PC_1_out(id_ex_1_pc_1_out),
    .imm12_out(id_ex_1_imm12_out), .mem_RD_out(id_ex_1_mem_rd_out), .mem_WR_out(id_ex_1_mem_wr_out),
    .MemToReg_out(id_ex_1_memtoreg_out), .ALU_EN_out(id_ex_1_alu_en_out), .ALU_src_out(id_ex_1_alu_src_out),
    .LUI_out(id_ex_1_lui_out), .JUMP_out(id_ex_1_jump_out), .BEQ_out(id_ex_1_beq_out),
    .BNEQ_out(id_ex_1_bneq_out), .LH_LB_out(id_ex_1_lh_lb_out), .HALF_out(id_ex_1_half_out),
    .SIN_out(id_ex_1_sin_out), .imm12_out_2(id_ex_1_imm12_out_2), .input1_out(id_ex_1_input1_out),
    .input2_out(id_ex_1_input2_out), .imm6ext16_out(id_ex_1_imm6ext16_out),
    .opcode_in_2(id_ex_1_opcode_in_2), .func_out(id_ex_1_func_out), .reg_WR(control_1_reg_wr),
    .reg_WR_2(id_ex_1_reg_wr_2), .reg_dest_out(id_ex_1_reg_dest_out), .reg_dest(control_1_regdest),
    .bits3_5(if_id_1_instruction_out[5:3]), .bits3_5_out(id_ex_1_bits3_5_out),
    .bits6_8(if_id_1_instruction_out_2), .bits6_8_out(id_ex_1_bits6_8_out), .JAL(control_1_jal),
    .JAL_out(id_ex_1_jal_out));  // open: RS, RS_out
  ALU_CTRL alu_ctrl_1 (.opcode(id_ex_1_opcode_in_2), .func(id_ex_1_func_out), .op(alu_ctrl_1_op));
  Multiplexer #(.width(16), .enable("false")) multiplexer_3 (
    .in0(id_ex_1_input2_out), .in1(id_ex_1_imm6ext16_out), .out(multiplexer_3_out), .sel(id_ex_1_alu_src_out));
  Multiplexer #(.width(16), .enable("false")) multiplexer_4 (
    .in0(multiplexer_6_out), .in1(mem_wb_1_lui_res_out), .out(multiplexer_4_out), .sel(mem_wb_1_lui_2));
  LUI_VALUE_main main_1 (.imm12(id_ex_1_imm12_out_2), .shifted_imm(main_1_shifted_imm));
  Write_Reg_Control write_reg_control_1 (
    .bits_3_5(id_ex_1_bits3_5_out), .bits_6_8(id_ex_1_bits6_8_out), .WR_Reg(write_reg_control_1_wr_reg),
    .reg_dest(id_ex_1_reg_dest_out), .LUI(id_ex_1_lui_out), .JAL(id_ex_1_jal_out));
  ALU alu_1 (
    .input_1(id_ex_1_input1_out), .input_2(multiplexer_3_out), .alu_op(alu_ctrl_1_op),
    .\output (alu_1_output), .alu_en(id_ex_1_alu_en_out), .Zero_flag(alu_1_zero_flag));  // open: carry_out
  EX_MEM ex_mem_1 (
    .Target_address(id_ex_1_pc_1_out), .imm12(id_ex_1_imm12_out), .mem_RD(id_ex_1_mem_rd_out),
    .mem_WR(id_ex_1_mem_wr_out), .MemToReg(id_ex_1_memtoreg_out), .JUMP(id_ex_1_jump_out),
    .BEQ(id_ex_1_beq_out), .BNEQ(id_ex_1_bneq_out), .LH_LB(id_ex_1_lh_lb_out), .half(id_ex_1_half_out),
    .sin(id_ex_1_sin_out), .lui_shifted(main_1_shifted_imm), .res_in(alu_1_output),
    .storeValue_in(id_ex_1_input2_out), .CLK(clock_1_out), .PC_1_out(ex_mem_1_pc_1_out),
    .imm12_out(ex_mem_1_imm12_out), .mem_RD_out(ex_mem_1_mem_rd_out), .mem_WR_out(ex_mem_1_mem_wr_out),
    .MemToReg_out(ex_mem_1_memtoreg_out), .JUMP_out(ex_mem_1_jump_out), .BEQ_out(ex_mem_1_beq_out),
    .BNEQ_out(ex_mem_1_bneq_out), .LH_LB_out(ex_mem_1_lh_lb_out), .HALF_out(ex_mem_1_half_out),
    .SIN_out(ex_mem_1_sin_out), .lui_shifted_2(ex_mem_1_lui_shifted_2), .res_out(ex_mem_1_res_out),
    .storeValue_out(ex_mem_1_storevalue_out), .zero(alu_1_zero_flag), .zero_out(ex_mem_1_zero_out),
    .reg_WR(id_ex_1_reg_wr_2), .reg_WR_out(ex_mem_1_reg_wr_out), .Wr_reg_out(ex_mem_1_wr_reg_out),
    .Wr_reg(write_reg_control_1_wr_reg), .LUI(id_ex_1_lui_out), .LUI_2(ex_mem_1_lui_2));  // open: Rd, Rd_out
  next_pc_main main_2 (
    .incremented_pc(ex_mem_1_pc_1_out), .imm_12(ex_mem_1_imm12_out), .BEQ(ex_mem_1_beq_out),
    .BNE(ex_mem_1_bneq_out), .JUMP(ex_mem_1_jump_out), .target_addr(main_2_target_addr),
    .PC_SRC(main_2_pc_src), .ZERO(ex_mem_1_zero_out));
  Data_Mem data_mem_1 (
    .Address(ex_mem_1_res_out), .mem_RD(ex_mem_1_mem_rd_out), .mem_WR(ex_mem_1_mem_wr_out),
    .WriteData(main_3_inverse), .Output(data_mem_1_output), .clk(clock_1_out));
  SIN_main main_3 (.store_value(ex_mem_1_storevalue_out), .SIN(mem_wb_1_sin_out), .inverse(main_3_inverse));
  MEM_WB mem_wb_1 (
    .MemToReg(ex_mem_1_memtoreg_out), .LH_LB(ex_mem_1_lh_lb_out), .half(ex_mem_1_half_out),
    .sin(ex_mem_1_sin_out), .ALU_Res_in(ex_mem_1_res_out), .loadRes_in(data_mem_1_output), .CLK(clock_1_out),
    .MemToReg_out(mem_wb_1_memtoreg_out), .LH_LB_out(mem_wb_1_lh_lb_out), .HALF_out(mem_wb_1_half_out),
    .SIN_out(mem_wb_1_sin_out), .ALU_Res_out(mem_wb_1_alu_res_out), .loadRes_out(mem_wb_1_loadres_out),
    .reg_WR(ex_mem_1_reg_wr_out), .reg_WR_out(mem_wb_1_reg_wr_out), .Wr_reg_out(mem_wb_1_wr_reg_out),
    .Wr_reg(ex_mem_1_wr_reg_out), .LUI_Res_in(ex_mem_1_lui_shifted_2), .LUI_Res_out(mem_wb_1_lui_res_out),
    .LUI(ex_mem_1_lui_2), .LUI_2(mem_wb_1_lui_2));  // open: Rd, Rd_out
  Multiplexer #(.width(16), .enable("false")) multiplexer_5 (
    .in0(mem_wb_1_alu_res_out), .in1(mem_wb_1_loadres_out), .out(multiplexer_5_out),
    .sel(mem_wb_1_memtoreg_out));
  Multiplexer #(.width(16), .enable("false")) multiplexer_6 (
    .in0(multiplexer_5_out), .in1(main_4_lh_or_lb), .out(multiplexer_6_out), .sel(mem_wb_1_half_out));
  lh_lb_main main_4 (.lh_lb(mem_wb_1_lh_lb_out), .Load_Value(multiplexer_5_out), .lh_or_lb(main_4_lh_or_lb));

  // Notes on the sheet:
  //   next pc
  //   pc+1
  //   +1
  //   R-TYPE
  //   imm 12
  //   I-TYPE
  //   Rt
  //   OPCODE
  //   FUNC
  //   imm6
  //   pc+1
  //   LUI
  //   zero
  //   Reg(Rt)
  //   alu result
  //   load result
  //   load val
  //   lowr bye/half
  //   half
endmodule
