// Logisim project Forwarding Unit.circ as structural Verilog: 1 circuit, main circuit main
module main (
  input  EX_MEM_RegWrite,
  input  [2:0] EX_MEM_RegisterRd,
  input  [2:0] ID_EX_RegisterRs,
  input  [2:0] ID_EX_RegisterRt,
  input  MEM_WB_RegWrite,
  input  [2:0] MEM_WB_RegisterRd,
  output [1:0] ForwardA,
  output [1:0] forwardB
);

  wire and_1_out, and_2_out, and_3_out, and_4_out, comparator_1_eq, comparator_2_eq, comparator_3_eq,
       comparator_4_eq, comparator_5_eq, comparator_6_eq, not_1_out, not_2_out, not_3_out, not_4_out;

  Comparator #(.width(3), .mode("unsigned")) comparator_1 (
    .a(EX_MEM_RegisterRd), .b(3'b000), .eq(comparator_1_eq));  // open: gt, lt
  Comparator #(.width(3), .mode("unsigned")) comparator_2 (
    .a(EX_MEM_RegisterRd), .b(ID_EX_RegisterRs), .eq(comparator_2_eq));  // open: gt, lt
  Comparator #(.width(3), .mode("unsigned")) comparator_3 (
    .a(EX_MEM_RegisterRd), .b(ID_EX_RegisterRt), .eq(comparator_3_eq));  // open: gt, lt
  Comparator #(.width(3), .mode("unsigned")) comparator_4 (
    .a(MEM_WB_RegisterRd), .b(3'b000), .eq(comparator_4_eq));  // open: gt, lt
  not not_1 (not_1_out, comparator_4_eq);
  Comparator #(.width(3), .mode("unsigned")) comparator_5 (
    .a(MEM_WB_RegisterRd), .b(ID_EX_RegisterRs), .eq(comparator_5_eq));  // open: gt, lt
  Comparator #(.width(3), .mode("unsigned")) comparator_6 (
    .a(MEM_WB_RegisterRd), .b(ID_EX_RegisterRt), .eq(comparator_6_eq));  // open: gt, lt
  not not_2 (not_2_out, comparator_1_eq);
  not not_3 (not_3_out, comparator_2_eq);
  and and_1 (and_1_out, EX_MEM_RegWrite, not_2_out, comparator_2_eq);
  and and_2 (and_2_out, EX_MEM_RegWrite, not_2_out, comparator_3_eq);
  not not_4 (not_4_out, comparator_3_eq);
  and and_3 (and_3_out, MEM_WB_RegWrite, not_1_out, not_3_out, comparator_5_eq);
  and and_4 (and_4_out, MEM_WB_RegWrite, not_1_out, not_4_out, comparator_6_eq);
  or or_1 (ForwardA[1], 1'b0, and_1_out);
  or or_2 (forwardB[1], 1'b0, and_2_out);
  or or_3 (ForwardA[0], 1'b0, and_3_out);
  or or_4 (forwardB[0], 1'b0, and_4_out);

  // Notes on the sheet:
  //   EX Hazard
  //   MEM Hazard
  //   a= 10
  //   b=10
  //   a=01
  //   b=01
endmodule
