// Logisim project Hazard detection unit.circ as structural Verilog: 1 circuit, main circuit main
module main (
  input  ID_EX_MemRead,
  input  [2:0] ID_EX_RegisterRt,
  input  [2:0] IF_ID_RegisterRs,
  input  [2:0] IF_ID_RegisterRt,
  output stall
);

  wire comparator_1_eq, comparator_2_eq, or_1_out;

  Comparator #(.width(3)) comparator_1 (
    .a(ID_EX_RegisterRt), .b(IF_ID_RegisterRs), .eq(comparator_1_eq));  // open: gt, lt
  Comparator #(.width(3)) comparator_2 (
    .a(ID_EX_RegisterRt), .b(IF_ID_RegisterRt), .eq(comparator_2_eq));  // open: gt, lt
  or or_1 (or_1_out, comparator_1_eq, comparator_2_eq);
  and and_1 (stall, ID_EX_MemRead, or_1_out);

  // Notes on the sheet:
  //   see hazard detection unit reference for formula 
endmodule
