// Logisim project LUI_VALUE.circ as structural Verilog: 1 circuit, main circuit main
module main (
  input  [11:0] imm12,
  output [15:0] shifted_imm
);

  wire [11:0] shifter_1_out;

  Shifter #(.width(12)) shifter_1 (.in(imm12), .\dist (4'b0100), .out(shifter_1_out));
  assign shifted_imm = {{4{1'b0}}, shifter_1_out};  // Bit_Extender bit_extender_1
endmodule
