// Logisim project SIN.circ as structural Verilog: 1 circuit, main circuit main
module main (
  input  [15:0] store_value,
  input  SIN,
  output [15:0] inverse
);

  wire [3:0] multiplexer_1_out, multiplexer_2_out;
  wire [15:0] shifter_1_out, shifter_2_out;

  Multiplexer #(.width(4), .enable("false")) multiplexer_1 (
    .in0(4'b0000), .in1(4'b1000), .out(multiplexer_1_out), .sel(SIN));
  Multiplexer #(.width(4), .enable("false")) multiplexer_2 (
    .in0(4'b0000), .in1(4'b1000), .out(multiplexer_2_out), .sel(SIN));
  Shifter #(.width(16)) shifter_1 (.in(store_value), .\dist (multiplexer_1_out), .out(shifter_1_out));
  Shifter #(.width(16), .shift("lr")) shifter_2 (.in(store_value), .\dist (multiplexer_2_out), .out(shifter_2_out));
  assign inverse = shifter_1_out | shifter_2_out;  // OR_Gate or_1, 16 bits wide
endmodule
