// Logisim project Write-Register-CTRL.circ as structural Verilog: 1 circuit, main circuit Write Reg Control
module Write_Reg_Control (
  input  [2:0] bits_3_5,
  input  [2:0] bits_6_8,
  input  reg_dest,
  input  LUI,
  input  JAL,
  output [2:0] WR_Reg
);

  wire [2:0] multiplexer_1_out, multiplexer_2_out;

  Multiplexer #(.width(3), .enable("false")) multiplexer_1 (
    .in0(bits_6_8), .in1(bits_3_5), .out(multiplexer_1_out), .sel(reg_dest));
  Multiplexer #(.width(3), .enable("false")) multiplexer_2 (
    .in0(multiplexer_1_out), .in1(3'b001), .out(multiplexer_2_out), .sel(LUI));
  Multiplexer #(.width(3), .enable("false")) multiplexer_3 (
    .in0(multiplexer_2_out), .in1(3'b111), .out(WR_Reg), .sel(JAL));

  // Notes on the sheet:
  //   RD
endmodule
