// Logisim project buffers.circ as structural Verilog: 4 circuits, main circuit IF/ID
module IF_ID (
  input  [15:0] PC_1_in,
  input  [15:0] Instruction_in,
  input  CLK,
  output [15:0] PC_1_out,
  output [15:0] Instruction_out
);

  wire undriven, undriven_2;

  Register #(.width(16), .trigger("falling")) register_1 (
    .D(PC_1_in), .en(1'b1), .Q(PC_1_out), .clk(CLK), .clr(undriven));
  Register #(.width(16), .trigger("falling")) register_2 (
    .D(Instruction_in), .en(1'b1), .Q(Instruction_out), .clk(CLK), .clr(undriven_2));

  // Notes on the sheet:
  //   This is meant to be a enable, but since we dont have a hazard detection unit it will always enabled for the time being
endmodule

module ID_EX (
  input  [15:0] Target_address,
  input  [11:0] imm12,
  input  reg_WR,
  input  mem_RD,
  input  mem_WR,
  input  MemToReg,
  input  ALU_EN,
  input  ALU_src,
  input  LUI,
  input  JUMP,
  input  BEQ,
  input  BNEQ,
  input  reg_dest,
  input  LH_LB,
  input  half,
  input  sin,
  input  [11:0] imm12_2,
  input  [15:0] input1_in,
  input  [15:0] input2_in,
  input  [15:0] imm6ext16_in,
  input  [3:0] opcode_in,
  input  [2:0] func_in,
  input  [2:0] bits3_5,
  input  [2:0] bits6_8,
  input  [2:0] RS,
  input  JAL,
  input  CLK,
  output [15:0] PC_1_out,
  output [11:0] imm12_out,
  output reg_WR_2,
  output mem_RD_out,
  output mem_WR_out,
  output MemToReg_out,
  output ALU_EN_out,
  output ALU_src_out,
  output LUI_out,
  output JUMP_out,
  output BEQ_out,
  output BNEQ_out,
  output reg_dest_out,
  output LH_LB_out,
  output HALF_out,
  output SIN_out,
  output [11:0] imm12_out_2,
  output [15:0] input1_out,
  output [15:0] input2_out,
  output [15:0] imm6ext16_out,
  output [3:0] opcode_in_2,
  output [2:0] func_out,
  output [2:0] bits3_5_out,
  output [2:0] bits6_8_out,
  output [2:0] RS_out,
  output JAL_out
);

  wire undriven, undriven_2, undriven_3, undriven_4, undriven_5, undriven_6, undriven_7, undriven_8,
       undriven_9, undriven_10, undriven_11, undriven_12, undriven_13, undriven_14, undriven_15, undriven_16,
       undriven_17, undriven_18, undriven_19, undriven_20, undriven_21, undriven_22, undriven_23,
       undriven_24, undriven_25, undriven_26;

  Register #(.width(16), .trigger("falling")) register_1 (
    .D(Target_address), .en(1'b1), .Q(PC_1_out), .clk(CLK), .clr(undriven));
  Register #(.width(12), .trigger("falling")) register_2 (
    .D(imm12), .en(1'b1), .Q(imm12_out), .clk(CLK), .clr(undriven_2));
  Register #(.width(1), .trigger("falling")) register_3 (
    .D(reg_WR), .en(1'b1), .Q(reg_WR_2), .clk(CLK), .clr(undriven_3));
  Register #(.width(1), .trigger("falling")) register_4 (
    .D(mem_RD), .en(1'b1), .Q(mem_RD_out), .clk(CLK), .clr(undriven_4));
  Register #(.width(1), .trigger("falling")) register_5 (
    .D(mem_WR), .en(1'b1), .Q(mem_WR_out), .clk(CLK), .clr(undriven_5));
  Register #(.width(1), .trigger("falling")) register_6 (
    .D(MemToReg), .en(1'b1), .Q(MemToReg_out), .clk(CLK), .clr(undriven_6));
  Register #(.width(1), .trigger("falling")) register_7 (
    .D(ALU_EN), .en(1'b1), .Q(ALU_EN_out), .clk(CLK), .clr(undriven_7));
  Register #(.width(1), .trigger("falling")) register_8 (
    .D(ALU_src), .en(1'b1), .Q(ALU_src_out), .clk(CLK), .clr(undriven_8));
  Register #(.width(1), .trigger("falling")) register_9 (.D(LUI), .en(1'b1), .Q(LUI_out), .clk(CLK), .clr(undriven_9));
  Register #(.width(1), .trigger("falling")) register_10 (
    .D(JUMP), .en(1'b1), .Q(JUMP_out), .clk(CLK), .clr(undriven_10));
  Register #(.width(1), .trigger("falling")) register_11 (
    .D(BEQ), .en(1'b1), .Q(BEQ_out), .clk(CLK), .clr(undriven_11));
  Register #(.width(1), .trigger("falling")) register_12 (
    .D(BNEQ), .en(1'b1), .Q(BNEQ_out), .clk(CLK), .clr(undriven_12));
  Register #(.width(1), .trigger("falling")) register_13 (
    .D(reg_dest), .en(1'b1), .Q(reg_dest_out), .clk(CLK), .clr(undriven_13));
  Register #(.width(1), .trigger("falling")) register_14 (
    .D(LH_LB), .en(1'b1), .Q(LH_LB_out), .clk(CLK), .clr(undriven_14));
  Register #(.width(1), .trigger("falling")) register_15 (
    .D(half), .en(1'b1), .Q(HALF_out), .clk(CLK), .clr(undriven_15));
  Register #(.width(1), .trigger("falling")) register_16 (
    .D(sin), .en(1'b1), .Q(SIN_out), .clk(CLK), .clr(undriven_16));
  Register #(.width(12), .trigger("falling")) register_17 (
    .D(imm12_2), .en(1'b1), .Q(imm12_out_2), .clk(CLK), .clr(undriven_17));
  Register #(.width(16), .trigger("falling")) register_18 (
    .D(input1_in), .en(1'b1), .Q(input1_out), .clk(CLK), .clr(undriven_18));
  Register #(.width(16), .trigger("falling")) register_19 (
    .D(input2_in), .en(1'b1), .Q(input2_out), .clk(CLK), .clr(undriven_19));
  Register #(.width(16), .trigger("falling")) register_20 (
    .D(imm6ext16_in), .en(1'b1), .Q(imm6ext16_out), .clk(CLK), .clr(undriven_20));
  Register #(.width(4), .trigger("falling")) register_21 (
    .D(opcode_in), .en(1'b1), .Q(opcode_in_2), .clk(CLK), .clr(undriven_21));
  Register #(.width(3), .trigger("falling")) register_22 (
    .D(func_in), .en(1'b1), .Q(func_out), .clk(CLK), .clr(undriven_22));
  Register #(.width(3), .trigger("falling")) register_23 (
    .D(bits3_5), .en(1'b1), .Q(bits3_5_out), .clk(CLK), .clr(undriven_23));
  Register #(.width(3), .trigger("falling")) register_24 (
    .D(bits6_8), .en(1'b1), .Q(bits6_8_out), .clk(CLK), .clr(undriven_24));
  Register #(.width(3), .trigger("falling")) register_25 (.D(RS), .en(1'b1), .Q(RS_out), .clk(CLK), .clr(undriven_25));
  Register #(.width(1), .trigger("falling")) register_26 (
    .D(JAL), .en(1'b1), .Q(JAL_out), .clk(CLK), .clr(undriven_26));
endmodule

module EX_MEM (
  input  [15:0] Target_address,
  input  [11:0] imm12,
  input  reg_WR,
  input  mem_RD,
  input  mem_WR,
  input  MemToReg,
  input  LUI,
  input  JUMP,
  input  BEQ,
  input  BNEQ,
  input  LH_LB,
  input  half,
  input  sin,
  input  [15:0] lui_shifted,
  input  [15:0] res_in,
  input  [2:0] Rd,
  input  zero,
  input  [15:0] storeValue_in,
  input  [2:0] Wr_reg,
  input  CLK,
  output [15:0] PC_1_out,
  output [11:0] imm12_out,
  output reg_WR_out,
  output mem_RD_out,
  output mem_WR_out,
  output MemToReg_out,
  output LUI_2,
  output JUMP_out,
  output BEQ_out,
  output BNEQ_out,
  output LH_LB_out,
  output HALF_out,
  output SIN_out,
  output [15:0] lui_shifted_2,
  output [15:0] res_out,
  output [2:0] Rd_out,
  output zero_out,
  output [15:0] storeValue_out,
  output [2:0] Wr_reg_out
);

  wire undriven_2, undriven_3, undriven_4, undriven_5, undriven_6, undriven_7, undriven_8, undriven_9,
       undriven_10, undriven_11, undriven_12, undriven_13, undriven_14, undriven_15, undriven_16,
       undriven_17, undriven_18, undriven_19, undriven_20;
  wire [15:0] undriven;

  Register #(.width(16), .trigger("falling")) register_1 (
    .D(Target_address), .en(1'b1), .Q(PC_1_out), .clk(CLK), .clr(undriven_2));
  Register #(.width(12), .trigger("falling")) register_2 (
    .D(imm12), .en(1'b1), .Q(imm12_out), .clk(CLK), .clr(undriven_3));
  Register #(.width(1), .trigger("falling")) register_3 (
    .D(reg_WR), .en(1'b1), .Q(reg_WR_out), .clk(CLK), .clr(undriven_4));
  Register #(.width(1), .trigger("falling")) register_4 (
    .D(mem_RD), .en(1'b1), .Q(mem_RD_out), .clk(CLK), .clr(undriven_5));
  Register #(.width(1), .trigger("falling")) register_5 (
    .D(mem_WR), .en(1'b1), .Q(mem_WR_out), .clk(CLK), .clr(undriven_6));
  Register #(.width(1), .trigger("falling")) register_6 (
    .D(MemToReg), .en(1'b1), .Q(MemToReg_out), .clk(CLK), .clr(undriven_7));
  Register #(.width(1), .trigger("falling")) register_7 (.D(LUI), .en(1'b1), .Q(LUI_2), .clk(CLK), .clr(undriven_8));
  Register #(.width(1), .trigger("falling")) register_8 (
    .D(JUMP), .en(1'b1), .Q(JUMP_out), .clk(CLK), .clr(undriven_9));
  Register #(.width(1), .trigger("falling")) register_9 (.D(BEQ), .en(1'b1), .Q(BEQ_out), .clk(CLK), .clr(undriven_10));
  Register #(.width(1), .trigger("falling")) register_10 (
    .D(BNEQ), .en(1'b1), .Q(BNEQ_out), .clk(CLK), .clr(undriven_11));
  Register #(.width(1), .trigger("falling")) register_11 (
    .D(LH_LB), .en(1'b1), .Q(LH_LB_out), .clk(CLK), .clr(undriven_12));
  Register #(.width(1), .trigger("falling")) register_12 (
    .D(half), .en(1'b1), .Q(HALF_out), .clk(CLK), .clr(undriven_13));
  Register #(.width(1), .trigger("falling")) register_13 (
    .D(sin), .en(1'b1), .Q(SIN_out), .clk(CLK), .clr(undriven_14));
  Register #(.width(16), .trigger("falling")) register_14 (
    .D(lui_shifted), .en(1'b1), .Q(lui_shifted_2), .clk(CLK), .clr(undriven_15));
  Register #(.width(16), .trigger("falling")) register_15 (
    .D(res_in), .en(1'b1), .Q(res_out), .clk(CLK), .clr(undriven_16));
  Register #(.width(3), .trigger("falling")) register_16 (.D(Rd), .en(1'b1), .Q(Rd_out), .clk(CLK), .clr(undriven_17));
  Register #(.width(1), .trigger("falling")) register_17 (
    .D(zero), .en(1'b1), .Q(zero_out), .clk(CLK), .clr(undriven_18));
  Register #(.width(16), .trigger("falling")) register_18 (
    .D(undriven), .en(1'b1), .Q(storeValue_out), .clk(CLK), .clr(undriven_19));
  Register #(.width(3), .trigger("falling")) register_19 (
    .D(Wr_reg), .en(1'b1), .Q(Wr_reg_out), .clk(CLK), .clr(undriven_20));
endmodule

module MEM_WB (
  input  reg_WR,
  input  MemToReg,
  input  LUI,
  input  LH_LB,
  input  half,
  input  sin,
  input  [15:0] LUI_Res_in,
  input  [15:0] ALU_Res_in,
  input  [15:0] loadRes_in,
  input  [2:0] Rd,
  input  [2:0] Wr_reg,
  input  CLK,
  output reg_WR_out,
  output MemToReg_out,
  output LUI_2,
  output LH_LB_out,
  output HALF_out,
  output SIN_out,
  output [15:0] LUI_Res_out,
  output [15:0] ALU_Res_out,
  output [15:0] loadRes_out,
  output [2:0] Rd_out,
  output [2:0] Wr_reg_out
);

  wire undriven, undriven_2, undriven_3, undriven_4, undriven_5, undriven_6, undriven_7, undriven_8,
       undriven_9, undriven_10, undriven_11;

  Register #(.width(1), .trigger("falling")) register_1 (
    .D(reg_WR), .en(1'b1), .Q(reg_WR_out), .clk(CLK), .clr(undriven));
  Register #(.width(1), .trigger("falling")) register_2 (
    .D(MemToReg), .en(1'b1), .Q(MemToReg_out), .clk(CLK), .clr(undriven_2));
  Register #(.width(1), .trigger("falling")) register_3 (.D(LUI), .en(1'b1), .Q(LUI_2), .clk(CLK), .clr(undriven_3));
  Register #(.width(1), .trigger("falling")) register_4 (
    .D(LH_LB), .en(1'b1), .Q(LH_LB_out), .clk(CLK), .clr(undriven_4));
  Register #(.width(1), .trigger("falling")) register_5 (
    .D(half), .en(1'b1), .Q(HALF_out), .clk(CLK), .clr(undriven_5));
  Register #(.width(1), .trigger("falling")) register_6 (.D(sin), .en(1'b1), .Q(SIN_out), .clk(CLK), .clr(undriven_6));
  Register #(.width(16), .trigger("falling")) register_7 (
    .D(LUI_Res_in), .en(1'b1), .Q(LUI_Res_out), .clk(CLK), .clr(undriven_7));
  Register #(.width(16), .trigger("falling")) register_8 (
    .D(ALU_Res_in), .en(1'b1), .Q(ALU_Res_out), .clk(CLK), .clr(undriven_8));
  Register #(.width(16), .trigger("falling")) register_9 (
    .D(loadRes_in), .en(1'b1), .Q(loadRes_out), .clk(CLK), .clr(undriven_9));
  Register #(.width(3), .trigger("falling")) register_10 (.D(Rd), .en(1'b1), .Q(Rd_out), .clk(CLK), .clr(undriven_10));
  Register #(.width(3), .trigger("falling")) register_11 (
    .D(Wr_reg), .en(1'b1), .Q(Wr_reg_out), .clk(CLK), .clr(undriven_11));

  // Notes on the sheet:
  //   regdesr should be here but we have it immediately written to write reg
endmodule
