// Logisim project lh_lb.circ as structural Verilog: 1 circuit, main circuit main
module main (
  input  lh_lb,
  input  [15:0] Load_Value,
  output [15:0] lh_or_lb
);

  wire [15:0] multiplexer_1_out;

  Multiplexer #(.width(16), .enable("false")) multiplexer_1 (
    .in0(16'hf), .in1(16'hff), .out(multiplexer_1_out), .sel(lh_lb));
  assign lh_or_lb = multiplexer_1_out & Load_Value;  // AND_Gate and_1, 16 bits wide
endmodule
