// Logisim project memsAndReg.circ as structural Verilog: 3 circuits, main circuit Register File
module Register_File (
  input  [15:0] WriteData,
  input  [2:0] R1,
  input  [2:0] R2,
  input  reg_Wr,
  input  CLK,
  input  [2:0] Write_Register,
  output [15:0] Read_Data1,
  output [15:0] Read_Data2
);

  wire and_1_out, and_2_out, and_3_out, and_4_out, and_5_out, and_6_out, and_7_out, decoder_1_out0,
       decoder_1_out1, decoder_1_out2, decoder_1_out3, decoder_1_out4, decoder_1_out5, decoder_1_out6,
       decoder_1_out7;
  wire [15:0] register_1_q, register_2_q, register_3_q, register_4_q, register_5_q, register_6_q,
       register_7_q;

  Register #(.width(16)) register_1 (.D(WriteData), .en(and_1_out), .Q(register_1_q), .clk(CLK), .clr(1'b0));
  and and_1 (and_1_out, reg_Wr, decoder_1_out1);
  Register #(.width(16)) register_2 (.D(WriteData), .en(and_2_out), .Q(register_2_q), .clk(CLK), .clr(1'b0));
  and and_2 (and_2_out, reg_Wr, decoder_1_out2);
  Register #(.width(16)) register_3 (.D(WriteData), .en(and_3_out), .Q(register_3_q), .clk(CLK), .clr(1'b0));
  and and_3 (and_3_out, reg_Wr, decoder_1_out3);
  Decoder #(.select(3)) decoder_1 (
    .out0(decoder_1_out0), .out1(decoder_1_out1), .out2(decoder_1_out2), .out3(decoder_1_out3),
    .out4(decoder_1_out4), .out5(decoder_1_out5), .out6(decoder_1_out6), .out7(decoder_1_out7),
    .sel(Write_Register));  // open: en
  and and_4 (and_4_out, reg_Wr, decoder_1_out4);
  and and_5 (and_5_out, reg_Wr, decoder_1_out5);
  and and_6 (and_6_out, reg_Wr, decoder_1_out6);
  and and_7 (and_7_out, reg_Wr, decoder_1_out7);
  Register #(.width(16)) register_4 (.D(WriteData), .en(and_4_out), .Q(register_4_q), .clk(CLK), .clr(1'b0));
  Register #(.width(16)) register_5 (.D(WriteData), .en(and_5_out), .Q(register_5_q), .clk(CLK), .clr(1'b0));
  Register #(.width(16)) register_6 (.D(WriteData), .en(and_6_out), .Q(register_6_q), .clk(CLK), .clr(1'b0));
  Register #(.width(16)) register_7 (.D(WriteData), .en(and_7_out), .Q(register_7_q), .clk(CLK), .clr(1'b0));
  Multiplexer #(.select(3), .width(16)) multiplexer_1 (
    .in0({16{1'b0}}), .in1(register_1_q), .in2(register_2_q), .in3(register_3_q), .in4(register_4_q),
    .in5(register_5_q), .in6(register_6_q), .in7(register_7_q), .out(Read_Data1), .sel(R1));  // open: en
  Multiplexer #(.select(3), .width(16)) multiplexer_2 (
    .in0({16{1'b0}}), .in1(register_1_q), .in2(register_2_q), .in3(register_3_q), .in4(register_4_q),
    .in5(register_5_q), .in6(register_6_q), .in7(register_7_q), .out(Read_Data2), .sel(R2));  // open: en

  // Notes on the sheet:
  //   R0
  //   R1
endmodule

module Data_Mem (
  input  [15:0] Address,
  input  mem_RD,
  input  clk,
  input  mem_WR,
  input  [15:0] WriteData,
  output [15:0] Output
);

  wire not_1_out, xor_1_out;

  xor xor_1 (xor_1_out, mem_RD, mem_WR);
  RAM #(.addrWidth(16), .dataWidth(16)) ram_1 (
    .addr(Address), .data(Output), .sel(xor_1_out), .clk(clk), .ld(not_1_out), .clr(1'b0));
  not not_1 (not_1_out, mem_WR);
  assign Output = mem_WR ? WriteData : 16'bz;  // Controlled_Buffer controlled_buffer_1
endmodule

module Inst_Mem (
  input  [15:0] Read_Address,
  input  clk,
  output [15:0] Instruction
);

  RAM #(.addrWidth(16), .dataWidth(16)) ram_1 (
    .addr(Read_Address), .data(Instruction), .sel(1'b1), .clk(clk), .ld(1'b1), .clr(1'b0));

  // Notes on the sheet:
  //   clk: pull=down
endmodule
