// Logisim project next_pc.circ as structural Verilog: 1 circuit, main circuit main
module main (
  input  [15:0] incremented_pc,
  input  [11:0] imm_12,
  input  BEQ,
  input  BNE,
  input  JUMP,
  input  ZERO,
  output PC_SRC,
  output [15:0] target_addr
);

  wire and_1_out, and_2_out, not_1_out;
  wire [15:0] bit_extender_1_out, bit_extender_2_out, multiplexer_1_out;

  assign bit_extender_1_out = {{4{imm_12[11]}}, imm_12};  // Bit_Extender bit_extender_1
  assign bit_extender_2_out = {{10{imm_12[5]}}, imm_12[5:0]};  // Bit_Extender bit_extender_2
  Multiplexer #(.width(16), .enable("false")) multiplexer_1 (
    .in0(bit_extender_2_out), .in1(bit_extender_1_out), .out(multiplexer_1_out), .sel(JUMP));
  Adder #(.width(16)) adder_1 (.a(incremented_pc), .b(multiplexer_1_out), .out(target_addr));  // open: cin, cout
  and and_1 (and_1_out, not_1_out, BNE);
  not not_1 (not_1_out, ZERO);
  or or_1 (PC_SRC, and_1_out, JUMP, and_2_out);
  and and_2 (and_2_out, ZERO, BEQ);

  // Notes on the sheet:
  //   JUMP
  //   IF JUMP -> 12 BIT IMMEDIATE , ELSE WILL USE THE 6 BIT IMMEDIATE FROM I TYPE
  //   if bne, or beq, or jump, target is from this component, else from the regulare pc increment 
endmodule
